# Fritzing sketch E220_ESP32 (saved by Fritzing 1.0.1rc)
breadboards: 2

parts:
  M1 = DOIT Esp32 DevKit v1 (30 pins long, 11 pins width) [part_number=ESP32S-PIN30]
  Mod1 = ossoyoo-lora-module
  LLC1 = Logic Level Converter [package="Breakout board"]
  M2 = RioRand LM2596

nets:
  N1: M1.3V3, LLC1.LV
  N2: M1.GND, LLC1.L-GND
  N3: M1.D15, Mod1.AUX
  N4: M1.RX2, LLC1.LV4
  N5: M1.TX2, LLC1.LV1
  N6: M1.D19, Mod1.M0
  N7: M1.D21, Mod1.M1
  N8: Mod1.RXD, LLC1.HV1
  N9: Mod1.TXD, LLC1.HV4
  N10: Mod1.VCC, LLC1.HV, M2.Pin_3
  N11: Mod1.GND, LLC1.H-GND, M2.Pin_4

notes:
  - E220-900T30D
  - ESP32
  - Fonte: 5V
  - Conv. de nível lógico Bi-direcional 5V - 3V

custom parts:
  DOIT Esp32 DevKit v1 (30 pins long, 11 pins width): The DOIT Esp32 DevKit v1 is one of the development board created by DOIT to evaluate the ESP-WROOM-32 module. It is based on the ESP32 microcontroller that boasts Wifi, Bluetooth, Ethernet and Low Power support all in a single chip. (vanepp) made breadboard work, adjusted pin numbering and labels and reduced size of schematic and cleaned up pcb. This chip is 30pins long (2 x15) and 11 pins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
  ossoyoo-lora-module: Osoyoo Long Distance wireless transceiver Uart LoRa Module.
  Logic Level Converter: 5V to/from 3.3V logic level converter
